# Fritzing sketch FullAdder (saved by Fritzing 0.9.1b)
breadboards: 1

parts:
  Pi1 = Adafruit Pi Cobbler
  IC1 = IC, DIP package, 14 pins [chip_label=7408]
  IC2 = IC, DIP package, 14 pins [chip_label=7486]
  IC3 = IC, DIP package, 14 pins [chip_label=7432]

nets:
  N1: Pi1.5V0, IC1.pin14, IC2.pin14, IC3.pin14
  N2: Pi1.GND, IC1.pin7, IC2.pin7, IC3.pin7
  N3: Pi1.#4, IC1.pin1, IC2.pin4
  N4: Pi1.#17, IC1.pin5, IC2.pin2
  N5: Pi1.#22, IC1.pin4, IC2.pin1
  N6: Pi1.#23, IC2.pin6
  N7: Pi1.#24, IC3.pin3
  N8: IC1.pin2, IC2.pin3, IC2.pin5
  N9: IC1.pin3, IC3.pin2
  N10: IC1.pin6, IC3.pin1

custom parts:
  Adafruit Pi Cobbler: Adafruit Pi Cobbler GPIO Breakout for Raspberry Pi
